// Logisim project Lab4Checkpoint1.circ as structural Verilog: 8 circuits, main circuit main
module main (
  input  [31:0] Instruction
);

  wire CLK, SRC;
  wire [3:0] CTRL;
  wire [31:0] IMM, multiplexer_1_out, register_file_1_rdata1, register_file_1_rdata2, RESULT;

  Clock clock_1 (.out(CLK));
  assign IMM = {{20{Instruction[31]}}, Instruction[31:20]};  // Bit_Extender bit_extender_1
  register_file register_file_1 (
    .RReg1(Instruction[19:15]), .RReg2(Instruction[24:20]), .WData(RESULT), .Clock_in(CLK), .Write(1'b1),
    .WReg(Instruction[11:7]), .RData1(register_file_1_rdata1), .RData2(register_file_1_rdata2));
  ALU_Control alu_control_1 (
    .I30(Instruction[30]), .I14(Instruction[14]), .I13(Instruction[13]), .I12(Instruction[12]),
    .I6(Instruction[6]), .I5(Instruction[5]), .I4(Instruction[4]), .ALU_Ctrl3(CTRL[3]), .ALU_Ctrl2(CTRL[2]),
    .ALU_Ctrl1(CTRL[1]), .ALU_Ctrl0(CTRL[0]), .ALU_Src(SRC));
  Multiplexer #(.enable("false"), .width(32)) multiplexer_1 (
    .in0(register_file_1_rdata2), .in1(IMM), .out(multiplexer_1_out), .sel(SRC));
  ALU32 alu32_1 (.A(register_file_1_rdata1), .B(multiplexer_1_out), .ALU_Ctrl(CTRL), .R(RESULT));  // open: C_in, C_out

  // Other names for the same wires on the sheet: INS[31:0] = Instruction; OPCODE[6:0] = Instruction[6:0];
  //   I4 = Instruction[4]; I5 = Instruction[5]; I6 = Instruction[6]; RD[4:0] = Instruction[11:7];
  //   I12 = Instruction[12]; I13 = Instruction[13]; I14 = Instruction[14]; RS1[4:0] = Instruction[19:15];
  //   RS2[4:0] = Instruction[24:20]; I30 = Instruction[30]
endmodule

module ADDER1 (
  input  A,
  input  B,
  input  C_in,
  output S,
  output C_out
);

  wire and_1_out, and_2_out, xor_1_out;

  xor xor_1 (xor_1_out, A, B);
  xor xor_2 (S, xor_1_out, C_in);
  and and_1 (and_1_out, C_in, xor_1_out);
  and and_2 (and_2_out, B, A);
  or or_1 (C_out, and_1_out, and_2_out);

  // Other names for the same wires on the sheet: A1 = A; B1 = B; C1 = C_in
endmodule

module ALU1 (
  input  [3:0] ALU_Ctrl,
  input  A,
  input  B,
  input  C_in,
  output C_out,
  output R
);

  wire AB1, AB2, AB3, BF, CF, not_1_out, S1, SLL1, SRA1, SRL1;

  and AandB (AB1, A, B);
  or AorB (AB2, A, B);
  xor AxorB (AB3, A, B);
  Shifter #(.width(1)) shifter_1 (.in(A), .\dist (B), .out(SLL1));
  Shifter #(.shift("lr"), .width(1)) shifter_2 (.in(A), .\dist (B), .out(SRL1));
  Shifter #(.shift("ar"), .width(1)) shifter_3 (.in(A), .\dist (B), .out(SRA1));
  ADDER1 adder1_1 (.A(A), .B(BF), .C_in(CF), .S(S1), .C_out(C_out));
  not not_1 (not_1_out, B);
  Multiplexer #(.enable("false"), .select(4)) multiplexer_1 (
    .in0(AB1), .in1(AB2), .in2(AB3), .in3(S1), .in7(S1), .in8(SLL1), .in9(SRL1), .in10(SRA1), .out(R),
    .sel(ALU_Ctrl));  // open: in4, in5, in6, in11, in12, in13, in14, in15
  Multiplexer #(.enable("false"), .select(4)) multiplexer_2 (
    .in0(B), .in1(B), .in2(B), .in3(B), .in4(B), .in5(B), .in6(B), .in7(not_1_out), .in8(B), .in9(B),
    .in10(B), .in11(B), .in12(B), .in13(B), .in14(B), .in15(B), .out(BF), .sel(ALU_Ctrl));
  Multiplexer #(.enable("false"), .select(4)) multiplexer_3 (
    .in0(C_in), .in1(C_in), .in2(C_in), .in3(C_in), .in4(C_in), .in5(C_in), .in6(C_in), .in7(1'b1),
    .in8(C_in), .in9(C_in), .in10(C_in), .in11(C_in), .in12(C_in), .in13(C_in), .in14(C_in), .in15(C_in),
    .out(CF), .sel(ALU_Ctrl));

  // Other names for the same wires on the sheet: A1 = A; B1 = B; C1 = C_in; CTRL[3:0] = ALU_Ctrl
endmodule

module ALU4 (
  input  [3:0] A,
  input  [3:0] B,
  input  C_in,
  input  [3:0] ALU_Ctrl,
  output C_out,
  output [3:0] R
);

  wire C0, C1, C2;

  // ALU1 alu1_1: pin names not known; wires that end beside it: A[0], B[0], C_in, ALU_Ctrl, C0, R[0]
  // ALU1 alu1_2: pin names not known; wires that end beside it: A[1], B[1], C0, ALU_Ctrl, C1, R[1]
  // ALU1 alu1_3: pin names not known; wires that end beside it: A[2], B[2], C1, ALU_Ctrl, C2, R[2]
  // ALU1 alu1_4: pin names not known; wires that end beside it: A[3], B[3], C2, ALU_Ctrl, C_out, R[3]

  // Other names for the same wires on the sheet: C3 = C_out; CTRL[3:0] = ALU_Ctrl; CX = C_in
endmodule

module ALU16 (
  input  [15:0] A,
  input  [15:0] B,
  input  C_in,
  input  [3:0] ALU_Ctrl,
  output C_out,
  output [15:0] R
);

  wire C0, C1, C2;

  ALU4 alu4_1 (.A(A[3:0]), .B(B[3:0]), .C_in(C_in), .ALU_Ctrl(ALU_Ctrl), .C_out(C0), .R(R[3:0]));
  ALU4 alu4_2 (.A(A[7:4]), .B(B[7:4]), .C_in(C0), .ALU_Ctrl(ALU_Ctrl), .C_out(C1), .R(R[7:4]));
  ALU4 alu4_3 (.A(A[11:8]), .B(B[11:8]), .C_in(C1), .ALU_Ctrl(ALU_Ctrl), .C_out(C2), .R(R[11:8]));
  ALU4 alu4_4 (.A(A[15:12]), .B(B[15:12]), .C_in(C2), .ALU_Ctrl(ALU_Ctrl), .C_out(C_out), .R(R[15:12]));

  // Other names for the same wires on the sheet: a0[3:0] = A[3:0]; a1[3:0] = A[7:4]; a2[3:0] = A[11:8];
  //   a3[3:0] = A[15:12]; b0[3:0] = B[3:0]; b1[3:0] = B[7:4]; b2[3:0] = B[11:8]; b3[3:0] = B[15:12]; C3 = C_out;
  //   CTRL[3:0] = ALU_Ctrl; CX = C_in; R0[3:0] = R[3:0]; R1[3:0] = R[7:4]; R2[3:0] = R[11:8]; R3[3:0] = R[15:12]
endmodule

module ALU32 (
  input  [31:0] A,
  input  [31:0] B,
  input  C_in,
  input  [3:0] ALU_Ctrl,
  output [31:0] R,
  output C_out
);

  wire C0;

  ALU16 alu16_1 (.A(A[15:0]), .B(B[15:0]), .C_in(C_in), .ALU_Ctrl(ALU_Ctrl), .C_out(C0), .R(R[15:0]));
  ALU16 alu16_2 (.A(A[31:16]), .B(B[31:16]), .C_in(C0), .ALU_Ctrl(ALU_Ctrl), .C_out(C_out), .R(R[31:16]));

  // Other names for the same wires on the sheet: a0[15:0] = A[15:0]; a1[15:0] = A[31:16]; b0[15:0] = B[15:0];
  //   b1[15:0] = B[31:16]; C1 = C_out; CTRL[3:0] = ALU_Ctrl; CX = C_in; R0[15:0] = R[15:0]; R1[15:0] = R[31:16]
endmodule

module ALU_Control (
  input  I30,
  input  I14,
  input  I13,
  input  I12,
  input  I6,
  input  I5,
  input  I4,
  output ALU_Ctrl3,
  output ALU_Ctrl2,
  output ALU_Ctrl1,
  output ALU_Ctrl0,
  output ALU_Src
);

  wire and_1_out, and_2_out, and_3_out, and_5_out, and_6_out, and_7_out, and_8_out, and_9_out, and_10_out,
       and_11_out, and_12_out, and_13_out, and_14_out, and_15_out, and_16_out, and_17_out, not_1_out,
       not_2_out, not_3_out, not_4_out, not_5_out, not_6_out, not_7_out;

  not not_1 (not_1_out, I30);
  not not_2 (not_2_out, I14);
  not not_3 (not_3_out, I13);
  not not_4 (not_4_out, I12);
  not not_5 (not_5_out, I6);
  not not_6 (not_6_out, I5);
  not not_7 (not_7_out, I4);
  and and_1 (and_1_out, not_1_out, not_3_out, I12, not_5_out, I4);
  and and_2 (and_2_out, not_3_out, I12, not_5_out, not_6_out, I4);
  and and_3 (and_3_out, I14, not_3_out, I12, not_5_out, I4);
  and and_4 (ALU_Ctrl2, I30, not_2_out, not_3_out, not_4_out, not_5_out, I5, I4);
  and and_5 (and_5_out, not_1_out, not_3_out, not_4_out, not_5_out, I4);
  and and_6 (and_6_out, not_2_out, not_3_out, not_4_out, not_5_out, I4);
  and and_7 (and_7_out, not_3_out, not_4_out, not_5_out, not_6_out, I4);
  and and_8 (and_8_out, not_2_out, I13, not_4_out, not_5_out, not_7_out);
  and and_9 (and_9_out, I30, I14, not_3_out, I12, not_5_out, I4);
  and and_10 (and_10_out, not_2_out, not_3_out, not_4_out, not_5_out, I4);
  and and_11 (and_11_out, not_2_out, I13, not_4_out, not_5_out, not_7_out);
  and and_12 (and_12_out, not_1_out, I14, not_3_out, I12, not_5_out, I4);
  and and_13 (and_13_out, not_1_out, I14, I13, not_4_out, not_5_out, I4);
  and and_14 (and_14_out, I14, I13, not_4_out, not_5_out, not_6_out, I4);
  and and_15 (and_15_out, not_3_out, not_5_out, not_6_out, I4);
  and and_16 (and_16_out, not_2_out, I13, not_4_out, not_5_out, not_7_out);
  and and_17 (and_17_out, I14, not_5_out, not_6_out, I4);
  or or_1 (ALU_Ctrl3, and_1_out, and_2_out, and_3_out);
  or or_2 (ALU_Ctrl1, and_5_out, and_6_out, and_7_out, and_8_out, and_9_out);
  or or_3 (ALU_Ctrl0, and_10_out, and_11_out, and_12_out, and_13_out, and_14_out);
  or or_4 (ALU_Src, and_15_out, and_16_out, and_17_out);
endmodule

module register_file (
  input  [4:0] RReg1,
  input  [4:0] RReg2,
  input  [31:0] WData,
  input  Clock_in,
  input  Write,
  input  [4:0] WReg,
  output [31:0] RData1,
  output [31:0] RData2
);

  wire D0, D1, D2, D3, D4, D5, D6, D7, D8, D9, D10, D11, D12, D13, D14, D15, D16, D17, D18, D19, D20, D21,
       D22, D23, D24, D25, D26, D27, D28, D29, D30, D31, DW0, DW1, DW2, DW3, DW4, DW5, DW6, DW7, DW8, DW9,
       DW10, DW11, DW12, DW13, DW14, DW15, DW16, DW17, DW18, DW19, DW20, DW21, DW22, DW23, DW24, DW25, DW26,
       DW27, DW28, DW29, DW30, DW31, or_1_out, or_2_out, or_3_out, or_4_out, or_5_out, or_6_out, or_7_out,
       or_8_out, or_9_out, or_10_out, or_11_out, or_12_out, or_13_out, or_14_out, or_15_out, or_16_out,
       or_17_out, or_18_out, or_19_out, or_20_out, or_21_out, or_22_out, or_23_out, or_24_out, or_25_out,
       or_26_out, or_27_out, or_28_out, or_29_out, or_30_out, or_31_out, or_32_out;
  wire [31:0] R0, R1, R2, R3, R4, R5, R6, R7, R8, R9, R10, R11, R12, R13, R14, R15, R16, R17, R18, R19, R20,
       R21, R22, R23, R24, R25, R26, R27, R28, R29, R30, R31;

  Bit_Extender #(.in_width(12), .out_width(32)) bit_extender_1 ();  // open: in, out
  Decoder #(.enable("false"), .select(5)) decoder_1 (
    .out0(D0), .out1(D1), .out2(D2), .out3(D3), .out4(D4), .out5(D5), .out6(D6), .out7(D7), .out8(D8),
    .out9(D9), .out10(D10), .out11(D11), .out12(D12), .out13(D13), .out14(D14), .out15(D15), .out16(D16),
    .out17(D17), .out18(D18), .out19(D19), .out20(D20), .out21(D21), .out22(D22), .out23(D23), .out24(D24),
    .out25(D25), .out26(D26), .out27(D27), .out28(D28), .out29(D29), .out30(D30), .out31(D31), .sel(WReg));
  and and_1 (DW0, D0, Write);
  and and_2 (DW1, D1, Write);
  and and_3 (DW2, D2, Write);
  and and_4 (DW3, D3, Write);
  and and_5 (DW4, D4, Write);
  and and_6 (DW5, D5, Write);
  and and_7 (DW6, D6, Write);
  and and_8 (DW7, D7, Write);
  and and_9 (DW8, D8, Write);
  and and_10 (DW9, D9, Write);
  and and_11 (DW10, D10, Write);
  and and_12 (DW11, D11, Write);
  and and_13 (DW12, D12, Write);
  and and_14 (DW13, D13, Write);
  and and_15 (DW14, D14, Write);
  and and_16 (DW15, D15, Write);
  and and_17 (DW16, D16, Write);
  and and_18 (DW17, D17, Write);
  and and_19 (DW18, D18, Write);
  and and_20 (DW19, D19, Write);
  and and_21 (DW20, D20, Write);
  and and_22 (DW21, D21, Write);
  and and_23 (DW22, D22, Write);
  and and_24 (DW23, D23, Write);
  and and_25 (DW24, D24, Write);
  and and_26 (DW25, D25, Write);
  and and_27 (DW26, D26, Write);
  and and_28 (DW27, D27, Write);
  and and_29 (DW28, D28, Write);
  and and_30 (DW29, D29, Write);
  and and_31 (DW30, D30, Write);
  and and_32 (DW31, D31, Write);
  Register #(.width(32)) register_1 (.D(WData), .clk(or_1_out), .Q(R0));  // open: en, clr
  or or_1 (or_1_out, Clock_in, DW0);
  Register #(.width(32)) register_2 (.D(WData), .clk(or_2_out), .Q(R1));  // open: en, clr
  or or_2 (or_2_out, Clock_in, DW1);
  Register #(.width(32)) register_3 (.D(WData), .clk(or_3_out), .Q(R2));  // open: en, clr
  or or_3 (or_3_out, Clock_in, DW2);
  Register #(.width(32)) register_4 (.D(WData), .clk(or_4_out), .Q(R3));  // open: en, clr
  or or_4 (or_4_out, Clock_in, DW3);
  Register #(.width(32)) register_5 (.D(WData), .clk(or_5_out), .Q(R4));  // open: en, clr
  or or_5 (or_5_out, Clock_in, DW4);
  Register #(.width(32)) register_6 (.D(WData), .clk(or_6_out), .Q(R5));  // open: en, clr
  or or_6 (or_6_out, Clock_in, DW5);
  Register #(.width(32)) register_7 (.D(WData), .clk(or_7_out), .Q(R6));  // open: en, clr
  or or_7 (or_7_out, Clock_in, DW6);
  Register #(.width(32)) register_8 (.D(WData), .clk(or_8_out), .Q(R7));  // open: en, clr
  or or_8 (or_8_out, Clock_in, DW7);
  Register #(.width(32)) register_9 (.D(WData), .clk(or_9_out), .Q(R8));  // open: en, clr
  or or_9 (or_9_out, Clock_in, DW8);
  Register #(.width(32)) register_10 (.D(WData), .clk(or_10_out), .Q(R9));  // open: en, clr
  or or_10 (or_10_out, Clock_in, DW9);
  Register #(.width(32)) register_11 (.D(WData), .clk(or_11_out), .Q(R10));  // open: en, clr
  or or_11 (or_11_out, Clock_in, DW10);
  Register #(.width(32)) register_12 (.D(WData), .clk(or_12_out), .Q(R11));  // open: en, clr
  or or_12 (or_12_out, Clock_in, DW11);
  Register #(.width(32)) register_13 (.D(WData), .clk(or_13_out), .Q(R12));  // open: en, clr
  or or_13 (or_13_out, Clock_in, DW12);
  Register #(.width(32)) register_14 (.D(WData), .clk(or_14_out), .Q(R13));  // open: en, clr
  or or_14 (or_14_out, Clock_in, DW13);
  Register #(.width(32)) register_15 (.D(WData), .clk(or_15_out), .Q(R14));  // open: en, clr
  or or_15 (or_15_out, Clock_in, DW14);
  Register #(.width(32)) register_16 (.D(WData), .clk(or_16_out), .Q(R15));  // open: en, clr
  or or_16 (or_16_out, Clock_in, DW15);
  Register #(.width(32)) register_17 (.D(WData), .clk(or_17_out), .Q(R16));  // open: en, clr
  or or_17 (or_17_out, Clock_in, DW16);
  Register #(.width(32)) register_18 (.D(WData), .clk(or_18_out), .Q(R17));  // open: en, clr
  or or_18 (or_18_out, Clock_in, DW17);
  Register #(.width(32)) register_19 (.D(WData), .clk(or_19_out), .Q(R18));  // open: en, clr
  or or_19 (or_19_out, Clock_in, DW18);
  Register #(.width(32)) register_20 (.D(WData), .clk(or_20_out), .Q(R19));  // open: en, clr
  or or_20 (or_20_out, Clock_in, DW19);
  Register #(.width(32)) register_21 (.D(WData), .clk(or_21_out), .Q(R20));  // open: en, clr
  or or_21 (or_21_out, Clock_in, DW20);
  Register #(.width(32)) register_22 (.D(WData), .clk(or_22_out), .Q(R21));  // open: en, clr
  or or_22 (or_22_out, Clock_in, DW21);
  Register #(.width(32)) register_23 (.D(WData), .clk(or_23_out), .Q(R22));  // open: en, clr
  or or_23 (or_23_out, Clock_in, DW22);
  Register #(.width(32)) register_24 (.D(WData), .clk(or_24_out), .Q(R23));  // open: en, clr
  or or_24 (or_24_out, Clock_in, DW23);
  Register #(.width(32)) register_25 (.D(WData), .clk(or_25_out), .Q(R24));  // open: en, clr
  or or_25 (or_25_out, Clock_in, DW24);
  Register #(.width(32)) register_26 (.D(WData), .clk(or_26_out), .Q(R25));  // open: en, clr
  or or_26 (or_26_out, Clock_in, DW25);
  Register #(.width(32)) register_27 (.D(WData), .clk(or_27_out), .Q(R26));  // open: en, clr
  or or_27 (or_27_out, Clock_in, DW26);
  Register #(.width(32)) register_28 (.D(WData), .clk(or_28_out), .Q(R27));  // open: en, clr
  or or_28 (or_28_out, Clock_in, DW27);
  Register #(.width(32)) register_29 (.D(WData), .clk(or_29_out), .Q(R28));  // open: en, clr
  or or_29 (or_29_out, Clock_in, DW28);
  Register #(.width(32)) register_30 (.D(WData), .clk(or_30_out), .Q(R29));  // open: en, clr
  or or_30 (or_30_out, Clock_in, DW29);
  Register #(.width(32)) register_31 (.D(WData), .clk(or_31_out), .Q(R30));  // open: en, clr
  or or_31 (or_31_out, Clock_in, DW30);
  Register #(.width(32)) register_32 (.D(WData), .clk(or_32_out), .Q(R31));  // open: en, clr
  or or_32 (or_32_out, Clock_in, DW31);
  Multiplexer #(.enable("false"), .select(5), .width(32)) multiplexer_1 (
    .in0(R0), .in1(R1), .in2(R2), .in3(R3), .in4(R4), .in5(R5), .in6(R6), .in7(R7), .in8(R8), .in9(R9),
    .in10(R10), .in11(R11), .in12(R12), .in13(R13), .in14(R14), .in15(R15), .in16(R16), .in17(R17),
    .in18(R18), .in19(R19), .in20(R20), .in21(R21), .in22(R22), .in23(R23), .in24(R24), .in25(R25),
    .in26(R26), .in27(R27), .in28(R28), .in29(R29), .in30(R30), .in31(R31), .out(RData1), .sel(RReg1));
  Multiplexer #(.enable("false"), .select(5), .width(32)) multiplexer_2 (
    .in0(R0), .in1(R1), .in2(R2), .in3(R3), .in4(R4), .in5(R5), .in6(R6), .in7(R7), .in8(R8), .in9(R9),
    .in10(R10), .in11(R11), .in12(R12), .in13(R13), .in14(R14), .in15(R15), .in16(R16), .in17(R17),
    .in18(R18), .in19(R19), .in20(R20), .in21(R21), .in22(R22), .in23(R23), .in24(R24), .in25(R25),
    .in26(R26), .in27(R27), .in28(R28), .in29(R29), .in30(R30), .in31(R31), .out(RData2), .sel(RReg2));

  // Other names for the same wires on the sheet: CLK = Clock_in; W1 = Write; WData1[31:0] = WData; WReg1[4:0] = WReg
endmodule
