// Logisim project Lab5VersionFinal.circ as structural Verilog: 12 circuits, main circuit main
module main (
);

  wire and_1_out, Branch, CLK, comparator_1_eq, I4, I5, I6, I12, I13, I14, I30, MemRead, MemtoReg, MemWrite,
       RegWrite, SRC;
  wire [3:0] CTRL;
  wire [31:0] adder_1_out, adder_2_out, D, IMM, INST, multiplexer_1_out, Q, RData1, RData2, ReadData, RESULT,
       WData;

  Register #(.width(32)) register_1 (.D(D), .en(1'b1), .clk(CLK), .Q(Q));  // open: clr
  Clock clock_1 (.out(CLK));
  InstructionMemory instructionmemory_1 (
    .Address(Q[23:0]), .ClockIn(CLK),
    .Instruction({INST[31], I30, INST[29:15], I14, I13, I12, INST[11:7], I6, I5, I4, INST[3:0]}));
  ImmGen immgen_1 (
    .Instruction({INST[31], I30, INST[29:15], I14, I13, I12, INST[11:7], I6, I5, I4, INST[3:0]}), .IMM32(IMM));
  Multiplexer #(.enable("false"), .width(32)) multiplexer_1 (
    .in0(RData2), .in1(IMM), .out(multiplexer_1_out), .sel(SRC));
  Control control_1 (
    .I6_0({I6, I5, I4, INST[3:0]}), .MemtoReg(MemtoReg), .RegWrite(RegWrite), .MemRead(MemRead),
    .MemWrite(MemWrite), .Branch(Branch));
  register_file register_file_1 (
    .RReg1(INST[19:15]), .RReg2(INST[24:20]), .WData(WData), .Clock_in(CLK), .Write(RegWrite),
    .WReg(INST[11:7]), .RData1(RData1), .RData2(RData2));
  ALU32 alu32_1 (.A(RData1), .B(multiplexer_1_out), .ALU_Ctrl(CTRL), .R(RESULT));  // open: C_in, C_out
  ALU_Control alu_control_1 (
    .I30(I30), .I14(I14), .I13(I13), .I12(I12), .I6(I6), .I5(I5), .I4(I4), .ALU_Ctrl3(CTRL[3]),
    .ALU_Ctrl2(CTRL[2]), .ALU_Ctrl1(CTRL[1]), .ALU_Ctrl0(CTRL[0]), .ALU_Src(SRC));
  Adder #(.width(32)) adder_1 (.a(Q), .b(32'h4), .out(adder_1_out));  // open: cin, cout
  Adder #(.width(32)) adder_2 (.a(Q), .b(IMM), .out(adder_2_out));  // open: cin, cout
  Comparator #(.width(32)) comparator_1 (.a(RData1), .b(RData2), .eq(comparator_1_eq));  // open: gt, lt
  Multiplexer #(.enable("false"), .width(32)) multiplexer_2 (.in0(RESULT), .in1(ReadData), .out(WData), .sel(MemtoReg));
  Multiplexer #(.enable("false"), .width(32)) multiplexer_3 (
    .in0(adder_1_out), .in1(adder_2_out), .out(D), .sel(and_1_out));
  and and_1 (and_1_out, Branch, comparator_1_eq);
  DataMemory datamemory_1 (
    .Address(RESULT[25:0]), .MemWrite(MemWrite), .MemRead(MemRead), .ClockIn(CLK), .WriteData(RData2),
    .ReadData(ReadData));

  // Other names for the same wires on the sheet: OPCODE[6:0] = {I6, I5, I4, INST[3:0]};
  //   INST (some bits) = {I30, I14, I13, I12, I6, I5, I4}; RD[4:0] = INST[11:7]; RS1[4:0] = INST[19:15];
  //   RS2[4:0] = INST[24:20]
endmodule

module ADDER1 (
  input  A,
  input  B,
  input  C_in,
  output S,
  output C_out
);

  wire and_1_out, and_2_out, xor_1_out;

  xor xor_1 (xor_1_out, A, B);
  xor xor_2 (S, xor_1_out, C_in);
  and and_1 (and_1_out, C_in, xor_1_out);
  and and_2 (and_2_out, B, A);
  or or_1 (C_out, and_1_out, and_2_out);

  // Other names for the same wires on the sheet: A1 = A; B1 = B; C1 = C_in
endmodule

module ALU1 (
  input  A,
  input  B,
  input  C_in,
  input  [3:0] ALU_Ctrl,
  output C_out,
  output R
);

  wire AB1, AB2, AB3, BF, CF, not_1_out, S1, SLL1, SRA1, SRL1;

  and AandB (AB1, A, B);
  or AorB (AB2, A, B);
  xor AxorB (AB3, A, B);
  Shifter #(.width(1)) shifter_1 (.in(A), .\dist (B), .out(SLL1));
  Shifter #(.shift("lr"), .width(1)) shifter_2 (.in(A), .\dist (B), .out(SRL1));
  Shifter #(.shift("ar"), .width(1)) shifter_3 (.in(A), .\dist (B), .out(SRA1));
  ADDER1 adder1_1 (.A(A), .B(BF), .C_in(CF), .S(S1), .C_out(C_out));
  not not_1 (not_1_out, B);
  Multiplexer #(.enable("false"), .select(4)) multiplexer_1 (
    .in0(AB1), .in1(AB2), .in2(AB3), .in3(S1), .in7(S1), .in8(SLL1), .in9(SRL1), .in10(SRA1), .out(R),
    .sel(ALU_Ctrl));  // open: in4, in5, in6, in11, in12, in13, in14, in15
  Multiplexer #(.enable("false"), .select(4)) multiplexer_2 (
    .in0(B), .in1(B), .in2(B), .in3(B), .in4(B), .in5(B), .in6(B), .in7(not_1_out), .in8(B), .in9(B),
    .in10(B), .in11(B), .in12(B), .in13(B), .in14(B), .in15(B), .out(BF), .sel(ALU_Ctrl));
  Multiplexer #(.enable("false"), .select(4)) multiplexer_3 (
    .in0(C_in), .in1(C_in), .in2(C_in), .in3(C_in), .in4(C_in), .in5(C_in), .in6(C_in), .in7(1'b1),
    .in8(C_in), .in9(C_in), .in10(C_in), .in11(C_in), .in12(C_in), .in13(C_in), .in14(C_in), .in15(C_in),
    .out(CF), .sel(ALU_Ctrl));

  // Other names for the same wires on the sheet: A1 = A; B1 = B; C1 = C_in; CTRL[3:0] = ALU_Ctrl
endmodule

module ALU4 (
  input  [3:0] A,
  input  [3:0] B,
  input  C_in,
  input  [3:0] ALU_Ctrl,
  output C_out,
  output [3:0] R
);

  wire C0, C1, C2;

  ALU1 alu1_1 (.A(A[0]), .B(B[0]), .C_in(C_in), .ALU_Ctrl(ALU_Ctrl), .C_out(C0), .R(R[0]));
  ALU1 alu1_2 (.A(A[1]), .B(B[1]), .C_in(C0), .ALU_Ctrl(ALU_Ctrl), .C_out(C1), .R(R[1]));
  ALU1 alu1_3 (.A(A[2]), .B(B[2]), .C_in(C1), .ALU_Ctrl(ALU_Ctrl), .C_out(C2), .R(R[2]));
  ALU1 alu1_4 (.A(A[3]), .B(B[3]), .C_in(C2), .ALU_Ctrl(ALU_Ctrl), .C_out(C_out), .R(R[3]));

  // Other names for the same wires on the sheet: C3 = C_out; CTRL[3:0] = ALU_Ctrl; CX = C_in
endmodule

module ALU16 (
  input  [15:0] A,
  input  [15:0] B,
  input  C_in,
  input  [3:0] ALU_Ctrl,
  output C_out,
  output [15:0] R
);

  wire C0, C1, C2;

  ALU4 alu4_1 (.A(A[3:0]), .B(B[3:0]), .C_in(C_in), .ALU_Ctrl(ALU_Ctrl), .C_out(C0), .R(R[3:0]));
  ALU4 alu4_2 (.A(A[7:4]), .B(B[7:4]), .C_in(C0), .ALU_Ctrl(ALU_Ctrl), .C_out(C1), .R(R[7:4]));
  ALU4 alu4_3 (.A(A[11:8]), .B(B[11:8]), .C_in(C1), .ALU_Ctrl(ALU_Ctrl), .C_out(C2), .R(R[11:8]));
  ALU4 alu4_4 (.A(A[15:12]), .B(B[15:12]), .C_in(C2), .ALU_Ctrl(ALU_Ctrl), .C_out(C_out), .R(R[15:12]));

  // Other names for the same wires on the sheet: a0[3:0] = A[3:0]; a1[3:0] = A[7:4]; a2[3:0] = A[11:8];
  //   a3[3:0] = A[15:12]; b0[3:0] = B[3:0]; b1[3:0] = B[7:4]; b2[3:0] = B[11:8]; b3[3:0] = B[15:12]; C3 = C_out;
  //   CTRL[3:0] = ALU_Ctrl; CX = C_in; R0[3:0] = R[3:0]; R1[3:0] = R[7:4]; R2[3:0] = R[11:8]; R3[3:0] = R[15:12]
endmodule

module ALU32 (
  input  [31:0] A,
  input  [31:0] B,
  input  C_in,
  input  [3:0] ALU_Ctrl,
  output [31:0] R,
  output C_out
);

  wire C0;

  ALU16 alu16_1 (.A(A[15:0]), .B(B[15:0]), .C_in(C_in), .ALU_Ctrl(ALU_Ctrl), .C_out(C0), .R(R[15:0]));
  ALU16 alu16_2 (.A(A[31:16]), .B(B[31:16]), .C_in(C0), .ALU_Ctrl(ALU_Ctrl), .C_out(C_out), .R(R[31:16]));

  // Other names for the same wires on the sheet: a0[15:0] = A[15:0]; a1[15:0] = A[31:16]; b0[15:0] = B[15:0];
  //   b1[15:0] = B[31:16]; C1 = C_out; CTRL[3:0] = ALU_Ctrl; CX = C_in; R0[15:0] = R[15:0]; R1[15:0] = R[31:16]
endmodule

module ALU_Control (
  input  I30,
  input  I14,
  input  I13,
  input  I12,
  input  I6,
  input  I5,
  input  I4,
  output ALU_Ctrl3,
  output ALU_Ctrl2,
  output ALU_Ctrl1,
  output ALU_Ctrl0,
  output ALU_Src
);

  wire and_1_out, and_2_out, and_3_out, and_5_out, and_6_out, and_7_out, and_8_out, and_9_out, and_10_out,
       and_11_out, and_12_out, and_13_out, and_14_out, and_15_out, and_16_out, and_17_out, not_1_out,
       not_2_out, not_3_out, not_4_out, not_5_out, not_6_out, not_7_out;

  not not_1 (not_1_out, I30);
  not not_2 (not_2_out, I14);
  not not_3 (not_3_out, I13);
  not not_4 (not_4_out, I12);
  not not_5 (not_5_out, I6);
  not not_6 (not_6_out, I5);
  not not_7 (not_7_out, I4);
  and and_1 (and_1_out, not_1_out, not_3_out, I12, not_5_out, I4);
  and and_2 (and_2_out, not_3_out, I12, not_5_out, not_6_out, I4);
  and and_3 (and_3_out, I14, not_3_out, I12, not_5_out, I4);
  and and_4 (ALU_Ctrl2, I30, not_2_out, not_3_out, not_4_out, not_5_out, I5, I4);
  and and_5 (and_5_out, not_1_out, not_3_out, not_4_out, not_5_out, I4);
  and and_6 (and_6_out, not_2_out, not_3_out, not_4_out, not_5_out, I4);
  and and_7 (and_7_out, not_3_out, not_4_out, not_5_out, not_6_out, I4);
  and and_8 (and_8_out, not_2_out, I13, not_4_out, not_5_out, not_7_out);
  and and_9 (and_9_out, I30, I14, not_3_out, I12, not_5_out, I4);
  and and_10 (and_10_out, not_2_out, not_3_out, not_4_out, not_5_out, I4);
  and and_11 (and_11_out, not_2_out, I13, not_4_out, not_5_out, not_7_out);
  and and_12 (and_12_out, not_1_out, I14, not_3_out, I12, not_5_out, I4);
  and and_13 (and_13_out, not_1_out, I14, I13, not_4_out, not_5_out, I4);
  and and_14 (and_14_out, I14, I13, not_4_out, not_5_out, not_6_out, I4);
  and and_15 (and_15_out, not_3_out, not_5_out, not_6_out, I4);
  and and_16 (and_16_out, not_2_out, I13, not_4_out, not_5_out, not_7_out);
  and and_17 (and_17_out, I14, not_5_out, not_6_out, I4);
  or or_1 (ALU_Ctrl3, and_1_out, and_2_out, and_3_out);
  or or_2 (ALU_Ctrl1, and_5_out, and_6_out, and_7_out, and_8_out, and_9_out);
  or or_3 (ALU_Ctrl0, and_10_out, and_11_out, and_12_out, and_13_out, and_14_out);
  or or_4 (ALU_Src, and_15_out, and_16_out, and_17_out);
endmodule

module register_file (
  input  [4:0] RReg1,
  input  [4:0] RReg2,
  input  [31:0] WData,
  input  Clock_in,
  input  Write,
  input  [4:0] WReg,
  output [31:0] RData1,
  output [31:0] RData2
);

  wire D0, D1, D2, D3, D4, D5, D6, D7, D8, D9, D10, D11, D12, D13, D14, D15, D16, D17, D18, D19, D20, D21,
       D22, D23, D24, D25, D26, D27, D28, D29, D30, D31, DW0, DW1, DW2, DW3, DW4, DW5, DW6, DW7, DW8, DW9,
       DW10, DW11, DW12, DW13, DW14, DW15, DW16, DW17, DW18, DW19, DW20, DW21, DW22, DW23, DW24, DW25, DW26,
       DW27, DW28, DW29, DW30, DW31;
  wire [31:0] R0, R1, R2, R3, R4, R5, R6, R7, R8, R9, R10, R11, R12, R13, R14, R15, R16, R17, R18, R19, R20,
       R21, R22, R23, R24, R25, R26, R27, R28, R29, R30, R31;

  Decoder #(.enable("false"), .select(5)) decoder_1 (
    .out0(D0), .out1(D1), .out2(D2), .out3(D3), .out4(D4), .out5(D5), .out6(D6), .out7(D7), .out8(D8),
    .out9(D9), .out10(D10), .out11(D11), .out12(D12), .out13(D13), .out14(D14), .out15(D15), .out16(D16),
    .out17(D17), .out18(D18), .out19(D19), .out20(D20), .out21(D21), .out22(D22), .out23(D23), .out24(D24),
    .out25(D25), .out26(D26), .out27(D27), .out28(D28), .out29(D29), .out30(D30), .out31(D31), .sel(WReg));
  and and_1 (DW0, D0, Write);
  and and_2 (DW1, D1, Write);
  and and_3 (DW2, D2, Write);
  and and_4 (DW3, D3, Write);
  and and_5 (DW4, D4, Write);
  and and_6 (DW5, D5, Write);
  and and_7 (DW6, D6, Write);
  and and_8 (DW7, D7, Write);
  and and_9 (DW8, D8, Write);
  and and_10 (DW9, D9, Write);
  and and_11 (DW10, D10, Write);
  and and_12 (DW11, D11, Write);
  and and_13 (DW12, D12, Write);
  and and_14 (DW13, D13, Write);
  and and_15 (DW14, D14, Write);
  and and_16 (DW15, D15, Write);
  and and_17 (DW16, D16, Write);
  and and_18 (DW17, D17, Write);
  and and_19 (DW18, D18, Write);
  and and_20 (DW19, D19, Write);
  and and_21 (DW20, D20, Write);
  and and_22 (DW21, D21, Write);
  and and_23 (DW22, D22, Write);
  and and_24 (DW23, D23, Write);
  and and_25 (DW24, D24, Write);
  and and_26 (DW25, D25, Write);
  and and_27 (DW26, D26, Write);
  and and_28 (DW27, D27, Write);
  and and_29 (DW28, D28, Write);
  and and_30 (DW29, D29, Write);
  and and_31 (DW30, D30, Write);
  and and_32 (DW31, D31, Write);
  Register #(.width(32)) register_1 (.D(WData), .en(DW0), .clk(Clock_in), .Q(R0), .clr(Write));
  Register #(.width(32)) register_2 (.D(WData), .en(DW1), .clk(Clock_in), .Q(R1));  // open: clr
  Register #(.width(32)) register_3 (.D(WData), .en(DW2), .clk(Clock_in), .Q(R2));  // open: clr
  Register #(.width(32)) register_4 (.D(WData), .en(DW3), .clk(Clock_in), .Q(R3));  // open: clr
  Register #(.width(32)) register_5 (.D(WData), .en(DW4), .clk(Clock_in), .Q(R4));  // open: clr
  Register #(.width(32)) register_6 (.D(WData), .en(DW5), .clk(Clock_in), .Q(R5));  // open: clr
  Register #(.width(32)) register_7 (.D(WData), .en(DW6), .clk(Clock_in), .Q(R6));  // open: clr
  Register #(.width(32)) register_8 (.D(WData), .en(DW7), .clk(Clock_in), .Q(R7));  // open: clr
  Register #(.width(32)) register_9 (.D(WData), .en(DW8), .clk(Clock_in), .Q(R8));  // open: clr
  Register #(.width(32)) register_10 (.D(WData), .en(DW9), .clk(Clock_in), .Q(R9));  // open: clr
  Register #(.width(32)) register_11 (.D(WData), .en(DW10), .clk(Clock_in), .Q(R10));  // open: clr
  Register #(.width(32)) register_12 (.D(WData), .en(DW11), .clk(Clock_in), .Q(R11));  // open: clr
  Register #(.width(32)) register_13 (.D(WData), .en(DW12), .clk(Clock_in), .Q(R12));  // open: clr
  Register #(.width(32)) register_14 (.D(WData), .en(DW13), .clk(Clock_in), .Q(R13));  // open: clr
  Register #(.width(32)) register_15 (.D(WData), .en(DW14), .clk(Clock_in), .Q(R14));  // open: clr
  Register #(.width(32)) register_16 (.D(WData), .en(DW15), .clk(Clock_in), .Q(R15));  // open: clr
  Register #(.width(32)) register_17 (.D(WData), .en(DW16), .clk(Clock_in), .Q(R16));  // open: clr
  Register #(.width(32)) register_18 (.D(WData), .en(DW17), .clk(Clock_in), .Q(R17));  // open: clr
  Register #(.width(32)) register_19 (.D(WData), .en(DW18), .clk(Clock_in), .Q(R18));  // open: clr
  Register #(.width(32)) register_20 (.D(WData), .en(DW19), .clk(Clock_in), .Q(R19));  // open: clr
  Register #(.width(32)) register_21 (.D(WData), .en(DW20), .clk(Clock_in), .Q(R20));  // open: clr
  Register #(.width(32)) register_22 (.D(WData), .en(DW21), .clk(Clock_in), .Q(R21));  // open: clr
  Register #(.width(32)) register_23 (.D(WData), .en(DW22), .clk(Clock_in), .Q(R22));  // open: clr
  Register #(.width(32)) register_24 (.D(WData), .en(DW23), .clk(Clock_in), .Q(R23));  // open: clr
  Register #(.width(32)) register_25 (.D(WData), .en(DW24), .clk(Clock_in), .Q(R24));  // open: clr
  Register #(.width(32)) register_26 (.D(WData), .en(DW25), .clk(Clock_in), .Q(R25));  // open: clr
  Register #(.width(32)) register_27 (.D(WData), .en(DW26), .clk(Clock_in), .Q(R26));  // open: clr
  Register #(.width(32)) register_28 (.D(WData), .en(DW27), .clk(Clock_in), .Q(R27));  // open: clr
  Register #(.width(32)) register_29 (.D(WData), .en(DW28), .clk(Clock_in), .Q(R28));  // open: clr
  Register #(.width(32)) register_30 (.D(WData), .en(DW29), .clk(Clock_in), .Q(R29));  // open: clr
  Register #(.width(32)) register_31 (.D(WData), .en(DW30), .clk(Clock_in), .Q(R30));  // open: clr
  Register #(.width(32)) register_32 (.D(WData), .en(DW31), .clk(Clock_in), .Q(R31));  // open: clr
  Multiplexer #(.enable("false"), .select(5), .width(32)) multiplexer_1 (
    .in0(R0), .in1(R1), .in2(R2), .in3(R3), .in4(R4), .in5(R5), .in6(R6), .in7(R7), .in8(R8), .in9(R9),
    .in10(R10), .in11(R11), .in12(R12), .in13(R13), .in14(R14), .in15(R15), .in16(R16), .in17(R17),
    .in18(R18), .in19(R19), .in20(R20), .in21(R21), .in22(R22), .in23(R23), .in24(R24), .in25(R25),
    .in26(R26), .in27(R27), .in28(R28), .in29(R29), .in30(R30), .in31(R31), .out(RData1), .sel(RReg1));
  Multiplexer #(.enable("false"), .select(5), .width(32)) multiplexer_2 (
    .in0(R0), .in1(R1), .in2(R2), .in3(R3), .in4(R4), .in5(R5), .in6(R6), .in7(R7), .in8(R8), .in9(R9),
    .in10(R10), .in11(R11), .in12(R12), .in13(R13), .in14(R14), .in15(R15), .in16(R16), .in17(R17),
    .in18(R18), .in19(R19), .in20(R20), .in21(R21), .in22(R22), .in23(R23), .in24(R24), .in25(R25),
    .in26(R26), .in27(R27), .in28(R28), .in29(R29), .in30(R30), .in31(R31), .out(RData2), .sel(RReg2));

  // Other names for the same wires on the sheet: CLK = Clock_in; W1 = Write; WData1[31:0] = WData; WReg1[4:0] = WReg
endmodule

module ImmGen (
  input  [31:0] Instruction,
  output [31:0] IMM32
);

  Multiplexer #(.enable("false"), .select(2)) multiplexer_1 (
    .in0(Instruction[20]), .in1(Instruction[7]), .in3(1'b0), .out(IMM32[0]), .sel(Instruction[6:5]));  // open: in2
  Multiplexer #(.enable("false"), .width(4)) multiplexer_2 (
    .in0(Instruction[24:21]), .in1(Instruction[11:8]), .out(IMM32[4:1]), .sel(Instruction[5]));
  Multiplexer #(.enable("false")) multiplexer_3 (
    .in0(Instruction[31]), .in1(Instruction[7]), .out(IMM32[11]), .sel(Instruction[6]));
  assign IMM32[31:12] = {{19{Instruction[31]}}, Instruction[31]};  // Bit_Extender bit_extender_1

  assign IMM32[10:5] = Instruction[30:25];

  // Other names for the same wires on the sheet: IMM0 = IMM32[0]; IMM4_1[3:0] = IMM32[4:1];
  //   I30_25[5:0] = Instruction[30:25]; IMM11 = IMM32[11]; IMM31_12[19:0] = IMM32[31:12]; I5 = Instruction[5];
  //   I6_5[1:0] = Instruction[6:5]; I6 = Instruction[6]; I7 = Instruction[7]; I11_8[3:0] = Instruction[11:8];
  //   I20 = Instruction[20]; I24_21[3:0] = Instruction[24:21]; I31 = Instruction[31]
endmodule

module Control (
  input  [6:0] I6_0,
  output MemtoReg,
  output RegWrite,
  output MemRead,
  output MemWrite,
  output Branch
);

  wire and_2_out, and_3_out, not_1_out, not_2_out, not_3_out, not_4_out, not_5_out;

  not not_1 (not_1_out, I6_0[6]);
  not not_2 (not_2_out, I6_0[5]);
  not not_3 (not_3_out, I6_0[4]);
  not not_4 (not_4_out, I6_0[3]);
  not not_5 (not_5_out, I6_0[2]);
  and and_1 (MemtoReg, not_1_out, not_3_out, not_4_out, not_5_out, I6_0[1], I6_0[0]);
  and and_2 (and_2_out, not_1_out, not_2_out, not_4_out, not_5_out, I6_0[1], I6_0[0]);
  and and_3 (and_3_out, not_1_out, I6_0[4], not_4_out, not_5_out, I6_0[1], I6_0[0]);
  and and_4 (MemRead, not_1_out, not_2_out, not_3_out, not_4_out, not_5_out, I6_0[1], I6_0[0]);
  and and_5 (MemWrite, not_1_out, I6_0[5], not_3_out, not_4_out, not_5_out, I6_0[1], I6_0[0]);
  and and_6 (Branch, I6_0[6], I6_0[5], not_3_out, not_4_out, not_5_out, I6_0[1], I6_0[0]);
  or or_1 (RegWrite, and_2_out, and_3_out);
endmodule

module InstructionMemory (
  input  [23:0] Address,
  input  ClockIn,
  output [31:0] Instruction
);

  wire not_1_out;

  not not_1 (not_1_out, ClockIn);
  RAM #(.addrWidth(22), .asyncread("true"), .dataWidth(32)) ram_1 (
    .addr(Address[23:2]), .we(1'b0), .oe(not_1_out), .dout(Instruction));  // open: clk, din
endmodule

module DataMemory (
  input  [25:0] Address,
  input  MemWrite,
  input  MemRead,
  input  ClockIn,
  input  [31:0] WriteData,
  output [31:0] ReadData
);

  RAM #(.addrWidth(24), .asyncread("true"), .dataWidth(32)) ram_1 (
    .addr(Address[25:2]), .we(MemWrite), .oe(MemRead), .clk(ClockIn), .din(WriteData), .dout(ReadData));
endmodule
